// Logisim project cpu24.circ as structural Verilog: 6 circuits, main circuit main_cpu
module main_cpu (
  input  RESET,
  input  ENABLE,
  input  CLK,
  output [23:0] CURR
);

  wire alu_1_halt, and_1_out, controlled_buffer_1_out;
  wire [7:0] rom_1_data;
  wire [23:0] a_q, alu_1_new_a, alu_1_new_b, alu_1_new_c, alu_1_next_instr, b_q, c_q, CNT_q;

  and and_1 (and_1_out, ~alu_1_halt, ENABLE);  // AND_Gate
  assign controlled_buffer_1_out = and_1_out ? CLK : 1'bz;  // Controlled_Buffer controlled_buffer_1
  Register #(.width(24), .trigger("falling")) a (
    .D(alu_1_new_a), .clk(controlled_buffer_1_out), .Q(a_q), .clr(RESET));  // open: en
  Register #(.width(24), .trigger("falling")) b (
    .D(alu_1_new_b), .clk(controlled_buffer_1_out), .Q(b_q), .clr(RESET));  // open: en
  Register #(.width(24), .trigger("falling")) c (
    .D(alu_1_new_c), .clk(controlled_buffer_1_out), .Q(c_q), .clr(RESET));  // open: en
  alu alu_1 (
    .CTRL(rom_1_data), .INSTR(CNT_q), .a(a_q), .b(b_q), .c(c_q), .HALT(alu_1_halt),
    .NEXT_INSTR(alu_1_next_instr), .new_a(alu_1_new_a), .new_b(alu_1_new_b), .new_c(alu_1_new_c), .CURR(CURR));
  Register #(.width(24), .trigger("falling")) CNT (
    .D(alu_1_next_instr), .en(ENABLE), .clk(controlled_buffer_1_out), .Q(CNT_q), .clr(RESET));
  ROM #(.addrWidth(24)) rom_1 (.addr(CNT_q), .data(rom_1_data));

  // Notes on the sheet:
  //   contents of rom_1 (hex, n*v repeats v):
  //   6*e7 ee 0 248*e7
  //   CPU 24 BITS
endmodule

module alu (
  input  [7:0] CTRL,
  input  [23:0] INSTR,
  input  [23:0] a,
  input  [23:0] b,
  input  [23:0] c,
  output HALT,
  output [23:0] NEXT_INSTR,
  output [23:0] new_a,
  output [23:0] new_b,
  output [23:0] new_c,
  output [23:0] CURR
);

  wire decoder_1_out1, decoder_1_out4, decoder_1_out5, decoder_1_out6, decoder_1_out7;
  wire [23:0] adder_1_out, and_1_out, divider_1_out, divider_2_rem, multiplier_1_out, negator_1_out,
       not_1_out, or_1_out, undriven, xor_1_out;

  Adder #(.width(24)) adder_1 (.a(a), .b(b), .out(adder_1_out));  // open: cin, cout
  assign xor_1_out = a ^ b;  // XOR_Gate xor_1, 24 bits wide
  assign or_1_out = a | b;  // OR_Gate or_1, 24 bits wide
  Multiplier #(.width(24)) multiplier_1 (.a(a), .b(b), .out(multiplier_1_out));  // open: cin, cout
  Divider #(.width(24)) divider_1 (.a(a), .b(b), .out(divider_1_out));  // open: upper, rem
  Divider #(.width(24)) divider_2 (.a(a), .b(b), .rem(divider_2_rem));  // open: out, upper
  assign not_1_out = ~a;  // NOT_Gate not_1, 24 bits wide
  Negator #(.width(24)) negator_1 (.in(a), .out(negator_1_out));
  assign and_1_out = a & b;  // AND_Gate and_1, 24 bits wide
  Multiplexer #(.select(5), .width(24), .enable("false")) multiplexer_1 (
    .in0({24{1'b0}}), .in1(adder_1_out), .in2(xor_1_out), .in3(or_1_out), .in4(multiplier_1_out),
    .in5(divider_1_out), .in6(divider_2_rem), .in7(not_1_out), .in8(negator_1_out), .in9(undriven), .in10(a),
    .in11(b), .in12(c), .in13(and_1_out), .in14({24{1'b0}}), .in15({24{1'b1}}), .out(CURR), .sel(CTRL[4:0]));  // open: in16, in17, in18, in19, in20, in21, in22, in23, in24, in25, in26, in27, in28, in29, in30, in31
  Decoder #(.select(3), .enable("false")) decoder_1 (
    .out0(HALT), .out1(decoder_1_out1), .out4(decoder_1_out4), .out5(decoder_1_out5), .out6(decoder_1_out6),
    .out7(decoder_1_out7), .sel({CTRL[5], CTRL[6], CTRL[7]}));  // open: out2, out3
  if_gate if_gate_1 (.i(decoder_1_out5), .t(CURR), .e(a), .o(new_a));
  if_gate if_gate_2 (.i(decoder_1_out6), .t(CURR), .e(b), .o(new_b));
  if_gate if_gate_3 (.i(decoder_1_out7), .t(CURR), .e(c), .o(new_c));
  jumping jumping_1 (
    .MODE(decoder_1_out4), .CTRL5(CTRL[4:0]), .a(a), .b(b), .c(c), .INSTR(INSTR), .NEXT_INSTR(NEXT_INSTR));
endmodule

module if_gate (
  input  i,
  input  [23:0] t,
  input  [23:0] e,
  output [23:0] o
);

  wire not_1_out;

  not not_1 (not_1_out, i);
  assign o = not_1_out ? e : 24'bz;  // Controlled_Buffer controlled_buffer_1
  assign o = i ? t : 24'bz;  // Controlled_Buffer controlled_buffer_2
endmodule

module if_gate_ex (
  input  [23:0] i,
  input  [23:0] t,
  input  [23:0] e,
  output [23:0] out_4
);

  wire comparator_1_eq, not_1_out;

  Comparator #(.width(24)) comparator_1 (.a({24{1'b0}}), .b(i), .eq(comparator_1_eq));  // open: gt, lt
  not not_1 (not_1_out, comparator_1_eq);
  assign out_4 = not_1_out ? t : 24'bz;  // Controlled_Buffer controlled_buffer_1
  assign out_4 = comparator_1_eq ? e : 24'bz;  // Controlled_Buffer controlled_buffer_2
endmodule

module jumping (
  input  MODE,
  input  [4:0] CTRL5,
  input  [23:0] a,
  input  [23:0] b,
  input  [23:0] c,
  input  [23:0] INSTR,
  output [23:0] NEXT_INSTR
);

  wire [23:0] adder_1_out, adder_2_out, if_gate_ex_1_out_4, if_gate_ex_2_out_4, multiplexer_1_out,
       subtractor_1_out;

  if_gate_ex if_gate_ex_1 (.i(a), .t(b), .e(adder_2_out), .out_4(if_gate_ex_1_out_4));
  if_gate_ex if_gate_ex_2 (.i(a), .t(b), .e(c), .out_4(if_gate_ex_2_out_4));
  Adder #(.width(24)) adder_1 (.a(INSTR), .b(a), .out(adder_1_out));  // open: cin, cout
  Subtractor #(.width(24)) subtractor_1 (.a(INSTR), .b(a), .out(subtractor_1_out));  // open: bin, bout
  Multiplexer #(.select(5), .width(24), .enable("false")) multiplexer_1 (
    .in0(a), .in1(if_gate_ex_1_out_4), .in2(if_gate_ex_2_out_4), .in3(adder_1_out), .in4(subtractor_1_out),
    .out(multiplexer_1_out), .sel(CTRL5));  // open: in5, in6, in7, in8, in9, in10, in11, in12, in13, in14, in15, in16, in17, in18, in19, in20, in21, in22, in23, in24, in25, in26, in27, in28, in29, in30, in31
  Adder #(.width(24)) adder_2 (.a(INSTR), .b(24'h1), .out(adder_2_out));  // open: cin, cout
  if_gate if_gate_1 (.i(MODE), .t(multiplexer_1_out), .e(adder_2_out), .o(NEXT_INSTR));
endmodule

module cnt (
  input  R,
  input  LOAD,
  input  ENABLE,
  input  CLK,
  input  [23:0] DATA,
  output [23:0] O
);

  Counter #(.width(24), .max('hffffff), .trigger("falling")) counter_1 (
    .clr(R), .load(LOAD), .up(1'b1), .count(ENABLE), .clk(CLK), .D(DATA), .Q(O));  // open: carry
endmodule
